# Fritzing sketch AA_circuito (saved by Fritzing 0.8.7b)
breadboards: 1

parts:
  T1 = LM35 Temperature Sensor [package="TO92 [THT]"]
  Componente1 = Arduino Uno (Rev3)

nets:
  N1: T1.+Vs, Componente1.5V
  N2: T1.Vout, Componente1.A0
  GND: T1.GND, Componente1.GND
